// Logisim project labo4.circ as structural Verilog: 3 circuits, main circuit SHREGI_4BITS
module SHREGI_4BITS (
  input  D3,
  input  D2,
  input  D1,
  input  D0,
  input  [3:0] in_5,
  input  in_6,
  output Q3,
  output Q2,
  output Q1,
  output Q0
);

  wire and_1_out, and_2_out, multiplexer_1_out, multiplexer_2_out, multiplexer_3_out, multiplexer_4_out,
       not_1_out;
  wire [1:0] bitselector_1_out;

  BitSelector #(.width(4), .group(2)) bitselector_1 (.in(in_5), .out(bitselector_1_out), .sel(1'b0));
  not not_1 (not_1_out, bitselector_1_out[0]);
  and and_1 (and_1_out, bitselector_1_out[0], bitselector_1_out[1]);
  and and_2 (and_2_out, not_1_out, bitselector_1_out[1]);
  Multiplexer #(.select(2), .enable("false")) multiplexer_1 (
    .in0(and_1_out), .in1(Q2), .in2(D3), .in3(Q3), .out(multiplexer_1_out), .sel(bitselector_1_out));
  D_Flip_Flop d_ff_1 (.D(multiplexer_1_out), .clk(in_6), .Q(Q3));  // open: Qn, preset, reset
  Multiplexer #(.select(2), .enable("false")) multiplexer_2 (
    .in0(Q3), .in1(Q1), .in2(D2), .in3(Q2), .out(multiplexer_2_out), .sel(bitselector_1_out));
  D_Flip_Flop d_ff_2 (.D(multiplexer_2_out), .clk(in_6), .Q(Q2));  // open: Qn, preset, reset
  Multiplexer #(.select(2), .enable("false")) multiplexer_3 (
    .in0(Q2), .in1(Q0), .in2(D1), .in3(Q1), .out(multiplexer_3_out), .sel(bitselector_1_out));
  D_Flip_Flop d_ff_3 (.D(multiplexer_3_out), .clk(in_6), .Q(Q1));  // open: Qn, preset, reset
  Multiplexer #(.select(2), .enable("false")) multiplexer_4 (
    .in0(Q1), .in1(and_2_out), .in2(D0), .in3(Q0), .out(multiplexer_4_out), .sel(bitselector_1_out));
  D_Flip_Flop d_ff_4 (.D(multiplexer_4_out), .clk(in_6), .Q(Q0));  // open: Qn, preset, reset

  // Notes on the sheet:
  //   Attention, votre version de Logisim
  //   ne contient pas de tracker. Si vous
  //   enregistrez votre projet, toutes les
  //   informations du tracker seront
  //   définitivement effacées.
endmodule

module SHREGI_8BITS (
  input  [3:0] in_1,
  input  [7:0] in_2,
  output [7:0] out_3
);

  // SHREGI_4BITS shregi_4bits_1: pin names not known; wires that end beside it: in_2[0], in_2[1], in_2[2], in_2[3], in_1[1:0], out_3[7], out_3[6], out_3[5], out_3[4]
  // SHREGI_4BITS shregi_4bits_2: pin names not known; wires that end beside it: in_2[4], in_2[5], in_2[6], in_2[7], in_1[3:2], out_3[3], out_3[2], out_3[1], out_3[0]

  // Notes on the sheet:
  //   Attention, votre version de Logisim
  //   ne contient pas de tracker. Si vous
  //   enregistrez votre projet, toutes les
  //   informations du tracker seront
  //   définitivement effacées.
endmodule

module LFSR_4BITS (
  input  Q1,
  input  Q0,
  output out_3,
  output out_4,
  output out_5,
  output out_6,
  output out_7
);

  wire clock_1_out, d_ff_1_q, d_ff_2_q, d_ff_3_q, xor_1_out;

  Clock clock_1 (.out(clock_1_out));
  D_Flip_Flop d_ff_1 (.D(xor_1_out), .clk(clock_1_out), .Q(d_ff_1_q), .Qn(out_5));  // open: preset, reset
  xor xor_1 (xor_1_out, Q1, Q0);
  D_Flip_Flop d_ff_2 (.D(d_ff_1_q), .clk(clock_1_out), .Q(d_ff_2_q), .Qn(out_6));  // open: preset, reset
  D_Flip_Flop d_ff_3 (.D(d_ff_2_q), .clk(clock_1_out), .Q(d_ff_3_q), .Qn(out_7));  // open: preset, reset
  D_Flip_Flop d_ff_4 (.D(d_ff_3_q), .clk(clock_1_out), .Q(out_3), .Qn(out_4));  // open: preset, reset

  // Notes on the sheet:
  //   Attention, votre version de Logisim
  //   ne contient pas de tracker. Si vous
  //   enregistrez votre projet, toutes les
  //   informations du tracker seront
  //   définitivement effacées.
endmodule
